// Logisim project 2_1.circ as structural Verilog: 1 circuit, main circuit main
module main (
  input  A,
  input  B,
  input  C,
  output S,
  output Cout
);

  wire HC00_2_out, HC00_3_out, HC00_out, HC02_out, HC86_out, not_1_out, not_2_out, not_3_out;

  xor HC86 (HC86_out, A, B);
  nand HC00 (HC00_out, A, B);
  nand HC00_2 (HC00_2_out, A, C);
  not not_1 (not_1_out, HC00_out);
  not not_2 (not_2_out, HC00_2_out);
  xor HC86_2 (S, HC86_out, C);
  nand HC00_3 (HC00_3_out, B, C);
  not not_3 (not_3_out, HC00_3_out);
  nor HC02 (HC02_out, not_3_out, not_1_out, not_2_out);
  not not_4 (Cout, HC02_out);

  // Notes on the sheet:
  //   1
  //   2
  //   1
  //   2
  //   7
  //   8
  //   1
  //   HC04
  //   3
  //   9
  //   2
  //   4
  //   5
  //   5
  //   4
  //   6
  //   6
  //   HC04
  //   3
  //   4
  //   11
  //   12
  //   5
  //   13
  //   6
  //   HC04
endmodule
