// Logisim project 2_2_1.circ as structural Verilog: 2 circuits, main circuit main
module main (
  input  A,
  input  B,
  input  CIN,
  output Cout,
  output S
);

  wire n74hc139_1_y0_prime, n74hc139_1_y2_prime, n74hc139_1_y2_prime_2, n74hc139_1_y3_prime,
       n74hc139_1_y3_prime_2, not_1_out, undriven, undriven_2, undriven_3;

  not not_1 (not_1_out, A);
  _74HC139 u_74hc139_1 (
    .YCC(A), .G_prime(B), .G_prime_2(CIN), .A_2(undriven_3), .B(undriven), .B_2(undriven_2), .GND(1'b0),
    .Y0_prime(n74hc139_1_y0_prime), .Y0_prime_2(not_1_out), .Y1_prime(B), .Y1_prime_2(CIN),
    .Y2_prime(n74hc139_1_y2_prime), .Y3_prime(n74hc139_1_y3_prime), .Y2_prime_2(n74hc139_1_y2_prime_2),
    .Y3_prime_2(n74hc139_1_y3_prime_2));  // open: A
  nand nand_1 (Cout, undriven_3, undriven, n74hc139_1_y2_prime, n74hc139_1_y3_prime_2);
  nand nand_2 (S, n74hc139_1_y2_prime_2, n74hc139_1_y3_prime_2, n74hc139_1_y3_prime, undriven_2);
  // also tied to VCC on the sheet: n74hc139_1_y0_prime

  // Notes on the sheet:
  //   1
  //   2
  //   GND
  //   Vcc
  //   74HC139
endmodule

module _74HC139 (
  input  YCC,
  input  G_prime,
  input  G_prime_2,
  input  A,
  input  A_2,
  input  B,
  input  B_2,
  input  GND,
  output Y0_prime,
  output Y0_prime_2,
  output Y1_prime,
  output Y1_prime_2,
  output Y2_prime,
  output Y3_prime,
  output Y2_prime_2,
  output Y3_prime_2
);

  wire nand_1_out, nand_2_out, nand_3_out, nand_4_out, nand_5_out, nand_6_out, nand_7_out, nand_8_out,
       not_1_out, not_2_out, not_3_out, not_4_out, not_5_out, not_6_out, not_8_out, not_10_out, not_12_out,
       not_14_out, not_15_out, not_16_out, not_17_out, not_22_out, not_23_out, not_24_out, not_25_out,
       not_26_out;

  not not_1 (not_1_out, A);
  not not_2 (not_2_out, B);
  not not_3 (not_3_out, G_prime_2);
  not not_4 (not_4_out, not_1_out);
  not not_5 (not_5_out, not_2_out);
  nand nand_1 (nand_1_out, not_1_out, not_2_out, not_3_out);
  nand nand_2 (nand_2_out, not_4_out, not_2_out, not_3_out);
  nand nand_3 (nand_3_out, not_1_out, not_5_out, not_3_out);
  nand nand_4 (nand_4_out, not_4_out, not_5_out, not_3_out);
  nand nand_5 (nand_5_out, not_22_out, not_23_out, not_24_out);
  nand nand_6 (nand_6_out, not_25_out, not_23_out, not_24_out);
  nand nand_7 (nand_7_out, not_22_out, not_26_out, not_24_out);
  nand nand_8 (nand_8_out, not_25_out, not_26_out, not_24_out);
  not not_6 (not_6_out, nand_1_out);
  not not_7 (Y0_prime_2, not_6_out);
  not not_8 (not_8_out, nand_2_out);
  not not_9 (Y1_prime, not_8_out);
  not not_10 (not_10_out, nand_3_out);
  not not_11 (Y2_prime, not_10_out);
  not not_12 (not_12_out, nand_4_out);
  not not_13 (Y3_prime, not_12_out);
  not not_14 (not_14_out, nand_5_out);
  not not_15 (not_15_out, nand_6_out);
  not not_16 (not_16_out, nand_7_out);
  not not_17 (not_17_out, nand_8_out);
  not not_18 (Y0_prime, not_14_out);
  not not_19 (Y1_prime_2, not_15_out);
  not not_20 (Y2_prime_2, not_16_out);
  not not_21 (Y3_prime_2, not_17_out);
  not not_22 (not_22_out, A_2);
  not not_23 (not_23_out, B_2);
  not not_24 (not_24_out, G_prime);
  not not_25 (not_25_out, not_22_out);
  not not_26 (not_26_out, not_23_out);
endmodule
