// Logisim project 2_5.circ as structural Verilog: 1 circuit, main circuit main
module main (
  input  A,
  input  B,
  input  S1,
  input  S2,
  input  S3,
  output Y1,
  output Y2,
  output Y3
);

  wire nand_1_out, nand_2_out, nand_3_out, nand_4_out, nand_5_out, nand_6_out, nand_7_out, nand_8_out,
       not_1_out, not_2_out, not_3_out, not_4_out, not_5_out, not_6_out, not_7_out, not_8_out, not_9_out,
       not_10_out, not_11_out;

  not not_1 (not_1_out, A);
  not not_2 (not_2_out, B);
  not not_3 (not_3_out, A);
  not not_4 (not_4_out, S2);
  not not_5 (not_5_out, S2);
  not not_6 (not_6_out, S3);
  not not_7 (not_7_out, A);
  not not_8 (not_8_out, S1);
  not not_9 (not_9_out, S3);
  not not_10 (not_10_out, S1);
  not not_11 (not_11_out, S2);
  nand nand_1 (nand_1_out, not_1_out, not_2_out, S1);
  nand nand_2 (nand_2_out, not_3_out, S1, not_4_out);
  nand nand_3 (nand_3_out, S1, not_5_out, not_6_out);
  nand nand_4 (nand_4_out, not_7_out, not_8_out, S2);
  nand nand_5 (nand_5_out, B, S2);
  nand nand_6 (nand_6_out, A, S2, not_9_out);
  nand nand_7 (nand_7_out, not_10_out, not_11_out, S3);
  nand nand_8 (nand_8_out, A, S3);
  nand nand_9 (Y1, nand_1_out, nand_2_out, nand_3_out);
  nand nand_10 (Y2, nand_4_out, nand_5_out, nand_6_out);
  nand nand_11 (Y3, nand_7_out, nand_8_out);
endmodule
