// Logisim project exp4_1_1.circ as structural Verilog: 1 circuit, main circuit main
module main (
  input  X1,
  output Q0,
  output Q1,
  output [3:0] X4,
  output Q2,
  output out_6,
  output Q3
);

  wire and_1_out, button_1_out;

  Button button_1 (.out(button_1_out));
  Counter #(.width(4), .max('hf)) counter_1 (
    .load(X1), .D(X4), .count(1'b1), .Q({Q3, Q2, Q1, Q0}), .carry(out_6), .clk(button_1_out), .clr(and_1_out));
  and and_1 (and_1_out, Q3, Q2);

  // Notes on the sheet:
  //   常数1
  //   CLK
  //   （按钮模拟CLK信号）
endmodule
