// Logisim project exp4_1_2.circ as structural Verilog: 1 circuit, main circuit main
module main (
  input  [3:0] in_1,
  input  in_2,
  output Q0,
  output Q1,
  output Q2,
  output Q3
);

  wire and_1_out, button_1_out, nor_1_out, not_1_out, not_2_out, undriven;

  not not_1 (not_1_out, 1'b1);
  Button button_1 (.out(button_1_out));
  nor nor_1 (nor_1_out, and_1_out, not_1_out);
  and and_1 (and_1_out, Q3, Q2, Q1, not_2_out);
  Counter #(.width(4), .max('hf)) counter_1 (
    .load(and_1_out), .D(in_1), .count(nor_1_out), .Q({Q3, Q2, Q1, Q0}), .clk(button_1_out), .clr(undriven));  // open: carry
  not not_2 (not_2_out, Q0);

  // Notes on the sheet:
  //   固定输入0011
  //   常数1
  //   CLK
  //   用按钮模拟时钟信号
endmodule
