// Logisim project exp4_2.circ as structural Verilog: 1 circuit, main circuit main
module main (
  output out_1,
  output out_2,
  output out_3,
  output out_4,
  output out_5,
  output out_6,
  output out_7,
  output out_8,
  output out_9,
  output out_10,
  output out_11,
  output out_12
);

  wire clock_1_out, n74163_1_p1, n74163_1_p15, nand_2_out, nand_3_out, nor_1_out, not_1_out, not_2_out,
       not_3_out, not_4_out;

  Clock clock_1 (.out(clock_1_out));
  not not_1 (not_1_out, n74163_1_p1);
  // _74163 74163_1: pin names not known; wires that end beside it: n74163_1_p1, clock_1_out, 1'b0, 1'b0, 1'b0, 1'b0, 1'b1, 1'b0, 1'b1, out_4, out_3, out_2, out_1, 1'b1, n74163_1_p15
  not not_2 (not_2_out, nor_1_out);
  nor nor_1 (nor_1_out, n74163_1_p1, nand_2_out);
  nand nand_1 (n74163_1_p1, out_1, out_4);
  not not_3 (not_3_out, not_2_out);
  // _74163 74163_2: pin names not known; wires that end beside it: not_2_out, clock_1_out, 1'b0, 1'b0, 1'b0, 1'b0, not_1_out, 1'b0, 1'b1, out_8, out_7, out_6, out_5, not_1_out, n74163_1_p15
  nand nand_2 (nand_2_out, out_5, out_8);
  // _74163 74163_3: pin names not known; wires that end beside it: 1'b1, clock_1_out, 1'b0, 1'b0, 1'b0, 1'b0, not_3_out, 1'b0, 1'b1, out_12, out_11, out_10, out_9, not_3_out, n74163_1_p15
  not not_4 (not_4_out, nand_3_out);
  nand nand_3 (nand_3_out, out_12, out_5);
  nand nand_4 (n74163_1_p15, not_4_out, out_4);

  // Notes on the sheet:
  //   1
  //   2
  //   3
endmodule
