// Logisim project exp4_2_upgraded.circ as structural Verilog: 2 circuits, main circuit main
module main (
  output out_1,
  output out_2,
  output out_3,
  output out_4,
  output out_5,
  output out_6,
  output out_7,
  output out_8,
  output out_9,
  output out_10,
  output out_11,
  output out_12
);

  wire all_1_a, all_1_b, all_1_c, all_1_d, all_1_e, all_1_f, all_1_g, all_2_a, all_2_b, all_2_c, all_2_d,
       all_2_e, all_2_f, all_2_g, all_3_a, all_3_b, all_3_c, all_3_d, all_3_e, all_3_f, all_3_g,
       button_1_out, n74163_1_p1, n74163_1_p15, nand_2_out, nand_3_out, nor_1_out, not_1_out, not_2_out,
       not_3_out, not_4_out;

  Button button_1 (.out(button_1_out));
  all all_1 (
    .A3(out_1), .A2(out_2), .A1(out_3), .A0(out_4), .a(all_1_a), .b(all_1_b), .c(all_1_c), .d(all_1_d),
    .e(all_1_e), .f(all_1_f), .g(all_1_g));
  _7_Segment_Display u_7_segment_display_1 (
    .g(all_1_g), .f(all_1_f), .a(all_1_a), .b(all_1_b), .e(all_1_e), .d(all_1_d), .c(all_1_c));  // open: dp
  not not_1 (not_1_out, n74163_1_p1);
  // _74163 74163_1: pin names not known; wires that end beside it: n74163_1_p1, button_1_out, 1'b0, 1'b0, 1'b0, 1'b0, 1'b1, 1'b0, 1'b1, out_4, out_3, out_2, out_1, 1'b1, n74163_1_p15
  not not_2 (not_2_out, nor_1_out);
  nor nor_1 (nor_1_out, n74163_1_p1, nand_2_out);
  nand nand_1 (n74163_1_p1, out_1, out_4);
  not not_3 (not_3_out, not_2_out);
  // _74163 74163_2: pin names not known; wires that end beside it: not_2_out, button_1_out, 1'b0, 1'b0, 1'b0, 1'b0, not_1_out, 1'b0, 1'b1, out_8, out_7, out_6, out_5, not_1_out, n74163_1_p15
  all all_2 (
    .A3(out_5), .A2(out_6), .A1(out_7), .A0(out_8), .a(all_2_a), .b(all_2_b), .c(all_2_c), .d(all_2_d),
    .e(all_2_e), .f(all_2_f), .g(all_2_g));
  nand nand_2 (nand_2_out, out_5, out_8);
  _7_Segment_Display u_7_segment_display_2 (
    .g(all_2_g), .f(all_2_f), .a(all_2_a), .b(all_2_b), .e(all_2_e), .d(all_2_d), .c(all_2_c));  // open: dp
  // _74163 74163_3: pin names not known; wires that end beside it: 1'b1, button_1_out, 1'b0, 1'b0, 1'b0, 1'b0, not_3_out, 1'b0, 1'b1, out_12, out_11, out_10, out_9, not_3_out, n74163_1_p15
  all all_3 (
    .A3(out_9), .A2(out_10), .A1(out_11), .A0(out_12), .a(all_3_a), .b(all_3_b), .c(all_3_c), .d(all_3_d),
    .e(all_3_e), .f(all_3_f), .g(all_3_g));
  not not_4 (not_4_out, nand_3_out);
  nand nand_3 (nand_3_out, out_12, out_5);
  _7_Segment_Display u_7_segment_display_3 (
    .g(all_3_g), .f(all_3_f), .a(all_3_a), .b(all_3_b), .e(all_3_e), .d(all_3_d), .c(all_3_c));  // open: dp
  nand nand_4 (n74163_1_p15, not_4_out, out_4);

  // Notes on the sheet:
  //   1
  //   2
  //   3
endmodule

module all (
  input  A3,
  input  A2,
  input  A1,
  input  A0,
  output a,
  output b,
  output c,
  output d,
  output e,
  output f,
  output g
);

  wire nand_1_out, nand_2_out, nand_3_out, nand_4_out, nand_5_out, nand_6_out, nand_7_out, nand_8_out,
       nand_9_out, nand_10_out, nand_11_out, nand_12_out, nand_13_out, nand_14_out, nand_15_out, nand_16_out,
       nand_17_out, nand_18_out, nand_19_out, nand_20_out, nand_21_out, nand_22_out, nand_23_out,
       nand_24_out, nand_25_out, nand_26_out, nand_27_out, nand_29_out, nand_30_out, nand_31_out,
       nand_32_out, nand_33_out, nand_34_out, nand_35_out, nand_36_out, nand_37_out, nand_38_out,
       nand_39_out, nand_40_out, nand_41_out, nand_42_out, nand_43_out;

  nand nand_1 (nand_1_out, A2, A2);
  nand nand_2 (nand_2_out, A0, A0);
  nand nand_3 (nand_3_out, A1, A1);
  nand nand_4 (nand_4_out, A0, A0);
  nand nand_5 (nand_5_out, A0, A0);
  nand nand_6 (nand_6_out, A2, A2);
  nand nand_7 (nand_7_out, A2, A2);
  nand nand_8 (nand_8_out, A0, A0);
  nand nand_9 (nand_9_out, A2, A2);
  nand nand_10 (nand_10_out, A0, A0);
  nand nand_11 (nand_11_out, A1, A1);
  nand nand_12 (nand_12_out, A2, A2);
  nand nand_13 (nand_13_out, A0, A0);
  nand nand_14 (nand_14_out, A0, A0);
  nand nand_15 (nand_15_out, A1, A1);
  nand nand_16 (nand_16_out, A0, A0);
  nand nand_17 (nand_17_out, A1, A1);
  nand nand_18 (nand_18_out, A0, A0);
  nand nand_19 (nand_19_out, A2, A2);
  nand nand_20 (nand_20_out, A1, A1);
  nand nand_21 (nand_21_out, A0, A0);
  nand nand_22 (nand_22_out, nand_1_out, nand_2_out);
  nand nand_23 (nand_23_out, A1, A1);
  nand nand_24 (nand_24_out, A2, A0);
  nand nand_25 (nand_25_out, A3, A3);
  nand nand_26 (nand_26_out, nand_3_out, nand_4_out);
  nand nand_27 (nand_27_out, A1, A0);
  nand nand_28 (c, A1, nand_5_out, nand_6_out);
  nand nand_29 (nand_29_out, nand_7_out, nand_8_out);
  nand nand_30 (nand_30_out, nand_9_out, A1);
  nand nand_31 (nand_31_out, A1, nand_10_out);
  nand nand_32 (nand_32_out, A2, nand_11_out, A0);
  nand nand_33 (nand_33_out, A3, A3);
  nand nand_34 (nand_34_out, nand_12_out, nand_13_out);
  nand nand_35 (nand_35_out, A1, nand_14_out);
  nand nand_36 (nand_36_out, nand_15_out, nand_16_out);
  nand nand_37 (nand_37_out, A2, nand_17_out);
  nand nand_38 (nand_38_out, A2, nand_18_out);
  nand nand_39 (nand_39_out, A3, A3);
  nand nand_40 (nand_40_out, nand_19_out, A1);
  nand nand_41 (nand_41_out, A2, nand_20_out);
  nand nand_42 (nand_42_out, A2, nand_21_out);
  nand nand_43 (nand_43_out, A3, A3);
  nand nand_44 (a, nand_22_out, nand_23_out, nand_24_out, nand_25_out);
  nand nand_45 (b, A2, nand_26_out, nand_27_out);
  nand nand_46 (d, nand_29_out, nand_30_out, nand_31_out, nand_32_out, nand_33_out);
  nand nand_47 (e, nand_34_out, nand_35_out);
  nand nand_48 (f, nand_36_out, nand_37_out, nand_38_out, nand_39_out);
  nand nand_49 (g, nand_40_out, nand_41_out, nand_42_out, nand_43_out);
endmodule
