// Logisim project exp4_3.circ as structural Verilog: 2 circuits, main circuit main
module main (
);

  wire clock_1_out, n74194_1_out_9, n74194_1_out_10, n74194_1_out_11, n74194_1_out_12, n74194_1_out_13,
       n74194_1_out_16, nor_1_out, nor_2_out, nor_3_out, xor_1_out, xor_2_out;

  Clock clock_1 (.out(clock_1_out));
  _74194 u_74194_1 (
    .in_1(n74194_1_out_9), .in_2(n74194_1_out_16), .in_3(n74194_1_out_16), .in_4(n74194_1_out_16),
    .in_5(n74194_1_out_16), .in_6(n74194_1_out_16), .in_7(xor_2_out), .in_8(n74194_1_out_16),
    .out_9(n74194_1_out_9), .out_10(n74194_1_out_10), .out_11(n74194_1_out_11), .out_12(n74194_1_out_12),
    .out_13(n74194_1_out_13), .out_14(clock_1_out), .out_15(n74194_1_out_9), .out_16(n74194_1_out_16));
  nor nor_1 (nor_1_out, n74194_1_out_12, n74194_1_out_13);
  xor xor_1 (xor_1_out, n74194_1_out_10, n74194_1_out_11);
  nor nor_2 (nor_2_out, nor_1_out, nor_1_out);
  nor nor_3 (nor_3_out, n74194_1_out_11, nor_2_out);
  xor xor_2 (xor_2_out, xor_1_out, nor_3_out);
  // also tied to GND on the sheet: n74194_1_out_16
  // also tied to VCC on the sheet: n74194_1_out_9

  // Notes on the sheet:
  //   74HC194
endmodule

module _74194 (
  input  in_1,
  input  in_2,
  input  in_3,
  input  in_4,
  input  in_5,
  input  in_6,
  input  in_7,
  input  in_8,
  output out_9,
  output out_10,
  output out_11,
  output out_12,
  output out_13,
  output out_14,
  output out_15,
  output out_16
);


  // Notes on the sheet:
  //   模拟74194的12个接口
endmodule
