// Logisim project exp4_4.circ as structural Verilog: 1 circuit, main circuit main
module main (
  input  \清零端 
);

  wire and_1_out, button_1_out, nor_1_out, not_1_out, or_1_out, shift_register_1_out, shift_register_1_q0,
       shift_register_1_q1, shift_register_1_q2, shift_register_1_q3, shift_register_2_out, xor_1_out;

  Button button_1 (.out(button_1_out));
  Shift_Register #(.length(4)) shift_register_1 (
    .in(or_1_out), .clk(button_1_out), .out(shift_register_1_out), .clr(\清零端 ), .q0(shift_register_1_q0),
    .q1(shift_register_1_q1), .q2(shift_register_1_q2), .q3(shift_register_1_q3));  // open: shift, load, d0, d1, d2, d3
  Shift_Register #(.length(4)) shift_register_2 (
    .in(shift_register_1_out), .clk(button_1_out), .out(shift_register_2_out), .clr(\清零端 ));  // open: shift, load, d0, q0, d1, q1, d2, q2, d3, q3
  not not_1 (not_1_out, shift_register_1_q1);
  Shift_Register #(.length(2)) shift_register_3 (
    .in(shift_register_2_out), .clk(button_1_out), .clr(\清零端 ));  // open: shift, out, load, d0, q0, d1, q1
  xor xor_1 (xor_1_out, shift_register_1_q3, shift_register_1_q2);
  and and_1 (and_1_out, not_1_out, shift_register_1_q0);
  nor nor_1 (nor_1_out, shift_register_1_q3, shift_register_1_q2, shift_register_1_q0);
  or or_1 (or_1_out, xor_1_out, and_1_out, nor_1_out);

  // Notes on the sheet:
  //   按钮模拟时钟信号
endmodule
