// Logisim project exp4_think_7.circ as structural Verilog: 2 circuits, main circuit main
module main (
  input  LOAD,
  input  A,
  input  B,
  input  C,
  input  D,
  input  E,
  input  F,
  input  G,
  input  H,
  output OUTPUT
);

  wire clock_1_out, n74hc194_1_out_14;

  Clock clock_1 (.out(clock_1_out));
  _74HC194 u_74hc194_1 (
    .in_1(clock_1_out), .in_2(1'b1), .in_3(1'b1), .in_4(LOAD), .in_5(1'b0), .in_6(A), .in_7(B), .in_8(C),
    .in_9(D), .out_14(n74hc194_1_out_14));  // open: in_10, out_11, out_12, out_13
  _74HC194 u_74hc194_2 (
    .in_1(clock_1_out), .in_2(1'b1), .in_3(1'b1), .in_4(LOAD), .in_5(n74hc194_1_out_14), .in_6(E), .in_7(F),
    .in_8(G), .in_9(H), .out_14(OUTPUT));  // open: in_10, out_11, out_12, out_13

  // Notes on the sheet:
  //   CLK
  //   74HC194
  //   74HC194
endmodule

module _74HC194 (
  input  in_1,
  input  in_2,
  input  in_3,
  input  in_4,
  input  in_5,
  input  in_6,
  input  in_7,
  input  in_8,
  input  in_9,
  input  in_10,
  output out_11,
  output out_12,
  output out_13,
  output out_14
);
endmodule
